// Logisim project cmd.circ as structural Verilog: 3 circuits, main circuit main
module main (
);

  wire clock, not_1_out, reset;
  wire [6:0] bit_extender_1_out;
  wire [7:0] adder_1_out, multiplexer_1_out, multiplexer_2_out, PC_q, rom_1_data;
  wire [15:8] rom_1_data_2;

  Button button_1 (.out(reset));
  Clock clock_1 (.out(clock));
  // Probe on multiplexer_2_out
  Register PC (.D(multiplexer_2_out), .en(clock), .clk(clock), .Q(PC_q), .clr(reset));
  Multiplexer #(.enable("false"), .width(8)) multiplexer_1 (
    .in0({8{1'b0}}), .in1(rom_1_data), .out(multiplexer_1_out), .sel(not_1_out));
  not not_1 (not_1_out, rom_1_data_2[8]);
  Multiplexer #(.enable("false"), .width(8)) multiplexer_2 (
    .in0(rom_1_data), .in1(adder_1_out), .out(multiplexer_2_out), .sel(not_1_out));
  Adder adder_1 (.a(8'h1), .b(PC_q), .out(adder_1_out));  // open: cin, cout
  ROM #(.dataWidth(16)) rom_1 (.addr(PC_q), .data({rom_1_data_2, rom_1_data}));
  // Probe on adder_1_out
  // Probe on {rom_1_data_2, rom_1_data}
  Bit_Extender #(.out_width(7)) bit_extender_1 (.in(multiplexer_1_out), .out(bit_extender_1_out));
  Register register_1 ();  // open: D, en, clk, Q, clr
  TTY tty_1 (.data(bit_extender_1_out), .clk(clock), .clr(reset));  // open: we

  // Notes on the sheet:
  //   contents of rom_1 (hex, n*v repeats v):
  //   48 45 4c 4c 4f a 100 65 23 33 44 55 7*100
endmodule

module RegisterFile (
  input  [15:0] WriteData,
  input  [2:0] WriteReg,
  input  [2:0] ReadReg1,
  input  WriteEnable,
  input  [2:0] ReadReg2,
  input  clock,
  input  Clear,
  output [15:0] OutReg1,
  output [15:0] OutReg2
);

  wire decoder_1_out0, decoder_1_out1, decoder_1_out2, decoder_1_out3, decoder_1_out4, decoder_1_out5,
       decoder_1_out6, decoder_1_out7;
  wire [15:0] register_1_q, register_2_q, register_3_q, register_4_q, register_5_q, register_6_q,
       register_7_q, register_8_q;

  Decoder #(.select(3)) decoder_1 (
    .out0(decoder_1_out0), .out1(decoder_1_out1), .out2(decoder_1_out2), .out3(decoder_1_out3),
    .out4(decoder_1_out4), .out5(decoder_1_out5), .out6(decoder_1_out6), .out7(decoder_1_out7),
    .sel(WriteReg), .en(WriteEnable));
  Register #(.width(16)) register_1 (.D(WriteData), .en(decoder_1_out0), .clk(clock), .Q(register_1_q), .clr(Clear));
  Register #(.width(16)) register_2 (.D(WriteData), .en(decoder_1_out1), .clk(clock), .Q(register_2_q), .clr(Clear));
  Register #(.width(16)) register_3 (.D(WriteData), .en(decoder_1_out2), .clk(clock), .Q(register_3_q), .clr(Clear));
  Register #(.width(16)) register_4 (.D(WriteData), .en(decoder_1_out3), .clk(clock), .Q(register_4_q), .clr(Clear));
  Register #(.width(16)) register_5 (.D(WriteData), .en(decoder_1_out4), .clk(clock), .Q(register_5_q), .clr(Clear));
  Register #(.width(16)) register_6 (.D(WriteData), .en(decoder_1_out5), .clk(clock), .Q(register_6_q), .clr(Clear));
  Register #(.width(16)) register_7 (.D(WriteData), .en(decoder_1_out6), .clk(clock), .Q(register_7_q), .clr(Clear));
  Register #(.width(16)) register_8 (.D(WriteData), .en(decoder_1_out7), .clk(clock), .Q(register_8_q), .clr(Clear));
  Multiplexer #(.enable("false"), .select(3), .width(16)) multiplexer_1 (
    .in0(register_1_q), .in1(register_2_q), .in2(register_3_q), .in3(register_4_q), .in4(register_5_q),
    .in5(register_6_q), .in6(register_7_q), .in7(register_8_q), .out(OutReg1), .sel(ReadReg2));
  Multiplexer #(.enable("false"), .select(3), .width(16)) multiplexer_2 (
    .in0(register_1_q), .in1(register_2_q), .in2(register_3_q), .in3(register_4_q), .in4(register_5_q),
    .in5(register_6_q), .in6(register_7_q), .in7(register_8_q), .out(OutReg2), .sel(ReadReg1));
endmodule

module TestTestRegisterFiule (
  input  [15:0] in_1,
  input  [2:0] in_2,
  input  [2:0] in_3,
  input  in_4,
  input  [2:0] in_5,
  output [15:0] out_6,
  output [15:0] out_7
);

  wire clock_1_out;

  Clock clock_1 (.out(clock_1_out));
  RegisterFile registerfile_1 (
    .WriteData(in_1), .WriteReg(in_2), .ReadReg1(in_3), .WriteEnable(in_4), .ReadReg2(in_5),
    .clock(clock_1_out), .OutReg1(out_6), .OutReg2(out_7));  // open: Clear
endmodule
